# Fritzing sketch auto_curtain (saved by Fritzing 0.9.2b)
breadboards: 1

parts:
  元件1 = Arduino Uno (Rev3)
  M1 = DC Motor
  IC1 = H-Bridge [package=THT]
  VCC1 = 4 x AAA Battery Mount
  J1 = Infrared Proximity Sensor
  元件2 = blueIOT RevB

nets:
  N1: 元件1.D10_PWM/SS, IC1.1_2EN
  N2: 元件1.D11_PWM/MOSI, J1.Vout
  GND: 元件1.GND, IC1.GND1, IC1.GND2, IC1.GND3, IC1.GND4, VCC1.-, J1.GND, 元件2.GND
  N3: 元件1.D0/RX, 元件2.SCA/A4
  N4: 元件1.D1/TX, 元件2.SCL/A5
  N5: 元件1.D4, IC1.1A
  N6: 元件1.D7, IC1.2A
  5V: 元件1.5V, IC1.VCC1, J1.Vcc, 元件2.3V3
  N7: M1.pin_1, IC1.2Y
  N8: M1.pin_2, IC1.1Y
  N9: IC1.VCC2, VCC1.+
